// Logisim project collision.circ as structural Verilog: 1 circuit, main circuit main
module main (
  input  [4:0] in_1,
  input  [4:0] in_2,
  input  [4:0] in_3,
  input  [4:0] in_4,
  output [4:0] out_5,
  output [4:0] out_6,
  output [4:0] out_7,
  output [4:0] out_8,
  output [4:0] out_9,
  output [4:0] out_10
);

  wire and_1_out, and_2_out, and_3_out, and_4_out, and_5_out, and_6_out, and_7_out, and_8_out, and_9_out,
       and_10_out, clock_1_out, clock_2_out, demultiplexer_1_out0, demultiplexer_1_out1,
       demultiplexer_1_out2, demultiplexer_1_out3, demultiplexer_1_out4, demultiplexer_1_out5,
       demultiplexer_1_out6, demultiplexer_1_out7, demultiplexer_1_out8, demultiplexer_1_out9,
       demultiplexer_2_out0, demultiplexer_2_out1, demultiplexer_2_out2, demultiplexer_2_out3,
       demultiplexer_2_out4, demultiplexer_2_out5, demultiplexer_2_out6, demultiplexer_2_out7,
       demultiplexer_2_out8, demultiplexer_2_out9, nor_1_out, xor_1_out, xor_2_out, xor_3_out, xor_4_out,
       xor_5_out, xor_6_out, xor_7_out, xor_8_out, xor_9_out, xor_10_out;

  xor xor_1 (xor_1_out, demultiplexer_1_out0, demultiplexer_2_out0);
  Clock clock_1 (.out(clock_1_out));
  Divider #(.width(5)) divider_1 (.a(in_1), .b(in_2), .out(out_5), .rem(out_6));  // open: upper
  Divider #(.width(5)) divider_2 (.a(in_3), .b(in_4), .out(out_7), .rem(out_8));  // open: upper
  xor xor_2 (xor_2_out, demultiplexer_1_out2, demultiplexer_2_out2);
  xor xor_3 (xor_3_out, demultiplexer_1_out1, demultiplexer_2_out1);
  Register #(.width(5)) register_1 (.D(in_1), .Q(out_10), .clk(clock_1_out), .clr(nor_1_out));  // open: en
  xor xor_4 (xor_4_out, demultiplexer_1_out4, demultiplexer_2_out4);
  xor xor_5 (xor_5_out, demultiplexer_1_out3, demultiplexer_2_out3);
  xor xor_6 (xor_6_out, demultiplexer_1_out5, demultiplexer_2_out5);
  xor xor_7 (xor_7_out, demultiplexer_1_out6, demultiplexer_2_out6);
  nor nor_1 (nor_1_out, xor_1_out, xor_3_out, xor_2_out, xor_5_out, xor_6_out, xor_7_out, xor_9_out, xor_8_out, xor_10_out);
  xor xor_8 (xor_8_out, demultiplexer_1_out8, demultiplexer_2_out8);
  xor xor_9 (xor_9_out, demultiplexer_1_out7, demultiplexer_2_out7);
  Demultiplexer #(.select(4)) demultiplexer_1 (
    .out0(demultiplexer_1_out0), .out1(demultiplexer_1_out1), .out2(demultiplexer_1_out2),
    .out3(demultiplexer_1_out3), .out4(demultiplexer_1_out4), .out5(demultiplexer_1_out5),
    .out6(demultiplexer_1_out6), .out7(demultiplexer_1_out7), .out8(demultiplexer_1_out8),
    .out9(demultiplexer_1_out9), .in(1'b1), .sel(out_6[3:0]));  // open: out10, out11, out12, out13, out14, out15, en
  Demultiplexer #(.select(4)) demultiplexer_2 (
    .out0(demultiplexer_2_out0), .out1(demultiplexer_2_out1), .out2(demultiplexer_2_out2),
    .out3(demultiplexer_2_out3), .out4(demultiplexer_2_out4), .out5(demultiplexer_2_out5),
    .out6(demultiplexer_2_out6), .out7(demultiplexer_2_out7), .out8(demultiplexer_2_out8),
    .out9(demultiplexer_2_out9), .in(1'b1), .sel(out_8[3:0]));  // open: out10, out11, out12, out13, out14, out15, en
  xor xor_10 (xor_10_out, demultiplexer_1_out9, demultiplexer_2_out9);
  and and_1 (and_1_out, demultiplexer_1_out1, demultiplexer_2_out1);
  and and_2 (and_2_out, demultiplexer_1_out0, demultiplexer_2_out0);
  LED led_1 (.in(and_1_out));
  LED led_2 (.in(and_2_out));
  and and_3 (and_3_out, demultiplexer_1_out3, demultiplexer_2_out3);
  and and_4 (and_4_out, demultiplexer_1_out2, demultiplexer_2_out2);
  LED led_3 (.in(and_3_out));
  LED led_4 (.in(and_4_out));
  Register #(.width(5)) register_2 (.D(in_3), .Q(out_9), .clk(clock_2_out), .clr(nor_1_out));  // open: en
  Clock clock_2 (.out(clock_2_out));
  and and_5 (and_5_out, demultiplexer_1_out5, demultiplexer_2_out5);
  and and_6 (and_6_out, demultiplexer_1_out4, demultiplexer_2_out4);
  LED led_5 (.in(and_6_out));
  LED led_6 (.in(and_5_out));
  and and_7 (and_7_out, demultiplexer_1_out7, demultiplexer_2_out7);
  and and_8 (and_8_out, demultiplexer_1_out6, demultiplexer_2_out6);
  LED led_7 (.in(and_7_out));
  LED led_8 (.in(and_8_out));
  and and_9 (and_9_out, demultiplexer_1_out8, demultiplexer_2_out8);
  and and_10 (and_10_out, demultiplexer_1_out9, demultiplexer_2_out9);
  LED led_9 (.in(and_10_out));
  LED led_10 (.in(and_9_out));
endmodule
